# Fritzing sketch SunriseAlarmClock (saved by Fritzing 0.9.2b)
breadboards: 1

parts:
  Bauteil1 = Arduino Uno (Rev3)
  Encoder = ENCODER_RGB_CA [package=encoder_led_3]
  Grove1 = Grove OLED 128x96
  AC_Dimmer = mystery part, 4 pins [chip_label="AC Dimmer"]

nets:
  N1: Bauteil1.A4/SDA, Grove1.SDA
  N2: Bauteil1.A5/SCL, Grove1.SCL
  N3: Bauteil1.D2, AC_Dimmer.pin3
  N4: Bauteil1.D4, AC_Dimmer.pin4
  N5: Bauteil1.D5_PWM, Encoder.+
  N6: Bauteil1.D6_PWM, Encoder.-B
  N7: Bauteil1.D7, Encoder.A
  3V3: Bauteil1.3V3, Encoder.B, Grove1.VCC, AC_Dimmer.pin1
  GND: Bauteil1.GND, Encoder.C, Grove1.GND, AC_Dimmer.pin2
  N8: Encoder.-R, Encoder.-G
